# Fritzing sketch Generic CPS 498 Looper Schematic (saved by Fritzing 0.9.6b)
breadboards: 1

parts:
  U1 = ESP32S-HiLetgo [part_number=ESP32-DevBoard]
  Part1 = Breadboard Power Supply Board SMD
  1/4"_Guitar_Jack_Circuit_Out = AMPHENOL - ACJS-MHDR [package=ACJS-MHDR]
  1/4"_Guitar_Jack_Circuit_In = AMPHENOL - ACJS-MHDR [package=ACJS-MHDR]
  CH1_Relay = DS2Y-5-DC5V [part_number=DS2Y-5-DC5V]
  1/4"_Guitar_Jack_In_CH1 = AMPHENOL - ACJS-MHDR [package=ACJS-MHDR]
  1/4"_Guitar_Jack_out_CH1 = AMPHENOL - ACJS-MHDR [package=ACJS-MHDR]
  J1 = Power Jack [package=power_jack_slot]
  1/4"_Guitar_Jack_out_CH3 = AMPHENOL - ACJS-MHDR [package=ACJS-MHDR]
  1/4"_Guitar_Jack_out_CH2 = AMPHENOL - ACJS-MHDR [package=ACJS-MHDR]
  1/4"_Guitar_Jack_In_CH2 = AMPHENOL - ACJS-MHDR [package=ACJS-MHDR]
  1/4"_Guitar_Jack_In_CH4 = AMPHENOL - ACJS-MHDR [package=ACJS-MHDR]
  1/4"_Guitar_Jack_In_CH6 = AMPHENOL - ACJS-MHDR [package=ACJS-MHDR]
  1/4"_Guitar_Jack_out_CH5 = AMPHENOL - ACJS-MHDR [package=ACJS-MHDR]
  1/4"_Guitar_Jack_In_CH5 = AMPHENOL - ACJS-MHDR [package=ACJS-MHDR]
  1/4"_Guitar_Jack_out_CH4 = AMPHENOL - ACJS-MHDR [package=ACJS-MHDR]
  1/4"_Guitar_Jack_out_CH6 = AMPHENOL - ACJS-MHDR [package=ACJS-MHDR]
  1/4"_Guitar_Jack_In_CH3 = AMPHENOL - ACJS-MHDR [package=ACJS-MHDR]
  1/4"_Guitar_Jack_out_CH8 = AMPHENOL - ACJS-MHDR [package=ACJS-MHDR]
  1/4"_Guitar_Jack_In_CH8 = AMPHENOL - ACJS-MHDR [package=ACJS-MHDR]
  1/4"_Guitar_Jack_out_CH7 = AMPHENOL - ACJS-MHDR [package=ACJS-MHDR]
  CH7_Relay = DS2Y-5-DC5V [part_number=DS2Y-5-DC5V]
  CH8_Relay = DS2Y-5-DC5V [part_number=DS2Y-5-DC5V]
  1/4"_Guitar_Jack_In_CH7 = AMPHENOL - ACJS-MHDR [package=ACJS-MHDR]
  S6 = SWITCH-MOMENTARY-2 [package=tactile-switch-1101ne]
  S5 = SWITCH-MOMENTARY-2 [package=tactile-switch-1101ne]
  S4 = SWITCH-MOMENTARY-2 [package=tactile-switch-1101ne]
  S3 = SWITCH-MOMENTARY-2 [package=tactile-switch-1101ne]
  S2 = SWITCH-MOMENTARY-2 [package=tactile-switch-1101ne]
  S1 = SWITCH-MOMENTARY-2 [package=tactile-switch-1101ne]
  CH6_Relay = DS2Y-5-DC5V [part_number=DS2Y-5-DC5V]
  CH5_Relay = DS2Y-5-DC5V [part_number=DS2Y-5-DC5V]
  CH4_Relay = DS2Y-5-DC5V [part_number=DS2Y-5-DC5V]
  CH3_Relay = DS2Y-5-DC5V [part_number=DS2Y-5-DC5V]
  CH2_Relay = DS2Y-5-DC5V [part_number=DS2Y-5-DC5V]

nets:
  Btn3: U1.GPIO36, S3.2
  Btn4: U1.GPIO39, S4.2
  Btn1: U1.GPIO34, S1.2
  Btn2: U1.GPIO35, S2.2
  Relay 6: U1.GPIO25, CH6_Relay.1_+
  Relay 7: U1.GPIO26, CH7_Relay.1_+
  Relay 3: U1.GPIO27, U1.GPIO21, CH3_Relay.1_+
  Btn5: U1.GPIO14, S5.2
  GND: U1.GND, Part1.GND, CH1_Relay.16_-, J1.GNDBREAK, J1.GND, CH7_Relay.16_-, CH8_Relay.16_-, S6.1, S5.1, S4.1, S3.1, S2.1, S1.1, CH6_Relay.16_-, CH5_Relay.16_-, CH4_Relay.16_-, CH3_Relay.16_-, CH2_Relay.16_-
  5V: U1.VIN, Part1.VCC
  Btn6: U1.GPIO16, S6.2
  Relay 1: U1.GPIO18, CH1_Relay.1_+
  Relay 2: U1.GPIO19, CH2_Relay.1_+
  Relay 4: U1.GPIO22, CH4_Relay.1_+
  Relay 5: U1.GPIO23, CH5_Relay.1_+
  N1: Part1.VIN, J1.PWR
  Switcher Out GND: 1/4"_Guitar_Jack_Circuit_Out.Sleeve_(1), CH8_Relay.13_COM
  Switcher Out: 1/4"_Guitar_Jack_Circuit_Out.Ring_(2), 1/4"_Guitar_Jack_Circuit_Out.Tip_(3), CH8_Relay.4_COM
  Switcher Input GND: 1/4"_Guitar_Jack_Circuit_In.Sleeve_(1), CH1_Relay.11_N.C., 1/4"_Guitar_Jack_out_CH1.Sleeve_(1)
  Switcher Input: 1/4"_Guitar_Jack_Circuit_In.Ring_(2), 1/4"_Guitar_Jack_Circuit_In.Tip_(3), CH1_Relay.6_N.C., 1/4"_Guitar_Jack_out_CH1.Ring_(5), 1/4"_Guitar_Jack_out_CH1.Tip_(6)
  N2: CH1_Relay.8_N.O., 1/4"_Guitar_Jack_In_CH1.Ring_(5), 1/4"_Guitar_Jack_In_CH1.Tip_(6)
  Relay 2 Signal In: CH1_Relay.4_COM, 1/4"_Guitar_Jack_out_CH2.Ring_(5), 1/4"_Guitar_Jack_out_CH2.Tip_(6), CH2_Relay.6_N.C.
  Relay 2 Signal In GND: CH1_Relay.13_COM, 1/4"_Guitar_Jack_out_CH2.Sleeve_(1), CH2_Relay.11_N.C.
  N3: CH1_Relay.9_N.O., 1/4"_Guitar_Jack_In_CH1.Sleeve_(1)
  Relay 3 Signal In GND: 1/4"_Guitar_Jack_out_CH3.Sleeve_(1), CH3_Relay.11_N.C., CH2_Relay.13_COM
  Relay 3 Signal In: 1/4"_Guitar_Jack_out_CH3.Ring_(5), 1/4"_Guitar_Jack_out_CH3.Tip_(6), CH3_Relay.6_N.C., CH2_Relay.4_COM
  N4: 1/4"_Guitar_Jack_out_CH2.Ring_(2), 1/4"_Guitar_Jack_out_CH2.Tip_(3)
  N5: 1/4"_Guitar_Jack_In_CH2.Sleeve_(1), CH2_Relay.9_N.O.
  N6: 1/4"_Guitar_Jack_In_CH2.Ring_(2), 1/4"_Guitar_Jack_In_CH2.Tip_(3)
  N7: 1/4"_Guitar_Jack_In_CH2.Ring_(5), 1/4"_Guitar_Jack_In_CH2.Tip_(6), CH2_Relay.8_N.O.
  N8: 1/4"_Guitar_Jack_In_CH4.Sleeve_(1), CH4_Relay.9_N.O.
  N9: 1/4"_Guitar_Jack_In_CH4.Ring_(5), 1/4"_Guitar_Jack_In_CH4.Tip_(6), CH4_Relay.8_N.O.
  N10: 1/4"_Guitar_Jack_In_CH6.Sleeve_(1), CH6_Relay.9_N.O.
  N11: 1/4"_Guitar_Jack_In_CH6.Ring_(5), 1/4"_Guitar_Jack_In_CH6.Tip_(6), CH6_Relay.8_N.O.
  Relay 5 Signal In GND: 1/4"_Guitar_Jack_out_CH5.Sleeve_(1), CH5_Relay.11_N.C., CH4_Relay.13_COM
  Relay 5 Signal In: 1/4"_Guitar_Jack_out_CH5.Ring_(5), 1/4"_Guitar_Jack_out_CH5.Tip_(6), CH5_Relay.6_N.C., CH4_Relay.4_COM
  N12: 1/4"_Guitar_Jack_In_CH5.Sleeve_(1), CH5_Relay.9_N.O.
  N13: 1/4"_Guitar_Jack_In_CH5.Ring_(5), 1/4"_Guitar_Jack_In_CH5.Tip_(6), CH5_Relay.8_N.O.
  Relay 4 Signal In GND: 1/4"_Guitar_Jack_out_CH4.Sleeve_(1), CH4_Relay.11_N.C., CH3_Relay.13_COM
  Relay 4 Signal In: 1/4"_Guitar_Jack_out_CH4.Ring_(5), 1/4"_Guitar_Jack_out_CH4.Tip_(6), CH4_Relay.6_N.C., CH3_Relay.4_COM
  Relay 6 Signal In GND: 1/4"_Guitar_Jack_out_CH6.Sleeve_(1), CH6_Relay.11_N.C., CH5_Relay.13_COM
  Relay 6 Signal In: 1/4"_Guitar_Jack_out_CH6.Ring_(5), 1/4"_Guitar_Jack_out_CH6.Tip_(6), CH6_Relay.6_N.C., CH5_Relay.4_COM
  N14: 1/4"_Guitar_Jack_In_CH3.Sleeve_(1), CH3_Relay.9_N.O.
  N15: 1/4"_Guitar_Jack_In_CH3.Ring_(5), 1/4"_Guitar_Jack_In_CH3.Tip_(6), CH3_Relay.8_N.O.
  Relay 8 Signal In GND: 1/4"_Guitar_Jack_out_CH8.Sleeve_(1), CH7_Relay.13_COM, CH8_Relay.11_N.C.
  Relay 8 Signal In: 1/4"_Guitar_Jack_out_CH8.Ring_(5), 1/4"_Guitar_Jack_out_CH8.Tip_(6), CH7_Relay.4_COM, CH8_Relay.6_N.C.
  N16: 1/4"_Guitar_Jack_In_CH8.Sleeve_(1), CH8_Relay.9_N.O.
  N17: 1/4"_Guitar_Jack_In_CH8.Ring_(5), 1/4"_Guitar_Jack_In_CH8.Tip_(6), CH8_Relay.8_N.O.
  Relay 7 Signal In GND: 1/4"_Guitar_Jack_out_CH7.Sleeve_(1), CH7_Relay.11_N.C., CH6_Relay.13_COM
  Relay 7 Signal In: 1/4"_Guitar_Jack_out_CH7.Ring_(5), 1/4"_Guitar_Jack_out_CH7.Tip_(6), CH7_Relay.6_N.C., CH6_Relay.4_COM
  N18: CH7_Relay.8_N.O., 1/4"_Guitar_Jack_In_CH7.Ring_(5), 1/4"_Guitar_Jack_In_CH7.Tip_(6)
  N19: CH7_Relay.9_N.O., 1/4"_Guitar_Jack_In_CH7.Sleeve_(1)
  Relay 8: CH8_Relay.1_+

custom parts:
  ESP32S-HiLetgo: HiLetgo ESP-WROOM-32 ESP32 ESP-32S Development Board 2.4GHz Dual-Mode WiFi + Bluetooth Dual Cores Microcontroller The ESP32 integrated with Antenna switches, RF Balun, power amplifiers, low-noise amplifiers, filters, and management modules, and the entire solution occupies the least area of PCB. 2.4 GHz Wi-Fi plus Bluetooth dual-mode chip, with TSMC Ultra-low power consumption 40nm technology,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
